# Fritzing sketch AlarmaSeguridad (saved by Fritzing 0.9.3b)
breadboards: 1

parts:
  J1 = Piezo Speaker
  Part1 = Arduino Mega 2560 (Rev3)
  LED1 = LED - 5mm [color="Red (635nm)" package="5 mm [THT]"]
  R1 = Resistor [tolerance=±5% resistance=220 package=THT]
  LED2 = LED - 5mm [color="Blue (430nm)" package="5 mm [THT]"]
  R2 = Resistor [tolerance=±5% resistance=220 package=THT]
  R3 = Resistor [tolerance=±5% resistance=220 package=THT]
  R4 = Resistor [tolerance=±5% resistance=220 package=THT]
  LED3 = LED - 5mm [color="Green (555nm)" package="5 mm [THT]"]
  S1 = Reed switch [package=THT]

nets:
  N1: J1.pin1, Part1.D8_PWM
  N2: Part1.D18/TX1, R3.Pin_0, S1.pin_1
  N3: Part1.D11_PWM, LED1.anode
  N4: Part1.D10_PWM, LED2.anode
  N5: Part1.GND, R1.Pin_1, R2.Pin_1, R3.Pin_1, R4.Pin_1, S1.pin_2
  N6: Part1.D6_PWM, LED3.anode
  N7: LED1.cathode, R1.Pin_0
  N8: LED2.cathode, R2.Pin_0
  N9: R4.Pin_0, LED3.cathode
